// Logisim project Arqui.circ as structural Verilog: 7 circuits, main circuit main
module main (
  input  CIn,
  input  Entrada_A,
  input  Entrada_B,
  output out_4,
  output COut
);

  wire and_1_out, and_2_out, xor_1_out_3;

  XOR xor_1 (.in_1(Entrada_B), .in_2(Entrada_A), .out_3(xor_1_out_3));
  and and_1 (and_1_out, Entrada_A, Entrada_B);
  XOR xor_2 (.in_1(CIn), .in_2(xor_1_out_3), .out_3(out_4));
  and and_2 (and_2_out, CIn, xor_1_out_3);
  or or_1 (COut, and_2_out, and_1_out);
endmodule

module XOR (
  input  in_1,
  input  in_2,
  output out_3
);

  wire and_1_out, and_2_out, not_1_out, not_2_out;

  not not_1 (not_1_out, in_1);
  not not_2 (not_2_out, in_2);
  and and_1 (and_1_out, not_1_out, in_2);
  and and_2 (and_2_out, in_1, not_2_out);
  or or_1 (out_3, and_1_out, and_2_out);
endmodule

module ALU_1_bit (
  input  A,
  input  B,
  input  in_3,
  input  [1:0] in_4,
  output out_5,
  output out_6
);

  wire and_1_out, main_1_out_4, or_1_out;

  and and_1 (and_1_out, A, B);
  or or_1 (or_1_out, A, B);
  main main_1 (.Entrada_A(B), .Entrada_B(A), .out_4(main_1_out_4), .COut(out_6), .CIn(in_3));
  Multiplexer #(.select(2)) multiplexer_1 (
    .in0(and_1_out), .in1(or_1_out), .in2(main_1_out_4), .out(out_5), .sel(in_4));  // open: in3, en

  // Notes on the sheet:
  //   ALU 1-bit
endmodule

module ALU_8_bits (
  input  [7:0] in_1,
  input  in_2,
  input  [1:0] in_3,
  input  [7:0] in_4,
  output [7:0] out_5,
  output out_6
);

  wire alu_1_bit_1_out_6, alu_1_bit_2_out_6, alu_1_bit_3_out_6, alu_1_bit_4_out_6, alu_1_bit_5_out_6,
       alu_1_bit_6_out_6, alu_1_bit_7_out_6;

  ALU_1_bit alu_1_bit_1 (
    .out_5(out_5[0]), .A(in_1[0]), .B(in_4[0]), .in_3(in_2), .out_6(alu_1_bit_1_out_6), .in_4(in_3));
  ALU_1_bit alu_1_bit_2 (
    .out_5(out_5[1]), .A(in_1[1]), .B(in_4[1]), .in_3(alu_1_bit_1_out_6), .out_6(alu_1_bit_2_out_6),
    .in_4(in_3));
  ALU_1_bit alu_1_bit_3 (
    .out_5(out_5[2]), .A(in_1[2]), .B(in_4[2]), .in_3(alu_1_bit_2_out_6), .out_6(alu_1_bit_3_out_6),
    .in_4(in_3));
  ALU_1_bit alu_1_bit_4 (
    .out_5(out_5[3]), .A(in_1[3]), .B(in_4[3]), .in_3(alu_1_bit_3_out_6), .out_6(alu_1_bit_4_out_6),
    .in_4(in_3));
  ALU_1_bit alu_1_bit_5 (
    .out_5(out_5[4]), .A(in_1[4]), .B(in_4[4]), .in_3(alu_1_bit_4_out_6), .out_6(alu_1_bit_5_out_6),
    .in_4(in_3));
  ALU_1_bit alu_1_bit_6 (
    .out_5(out_5[5]), .A(in_1[5]), .B(in_4[5]), .in_3(alu_1_bit_5_out_6), .out_6(alu_1_bit_6_out_6),
    .in_4(in_3));
  ALU_1_bit alu_1_bit_7 (
    .out_5(out_5[6]), .A(in_1[6]), .B(in_4[6]), .in_3(alu_1_bit_6_out_6), .out_6(alu_1_bit_7_out_6),
    .in_4(in_3));
  ALU_1_bit alu_1_bit_8 (
    .out_5(out_5[7]), .A(in_1[7]), .B(in_4[7]), .in_3(alu_1_bit_7_out_6), .out_6(out_6), .in_4(in_3));
endmodule

module \ALU_1_bit_con_sustracción  (
  input  A,
  input  B,
  input  in_3,
  input  [1:0] in_4,
  output out_5,
  output out_6
);

  wire and_1_out, main_1_cout, main_1_out_4, main_2_cout, main_2_out_4, not_1_out, or_1_out;

  not not_1 (not_1_out, B);
  and and_1 (and_1_out, A, B);
  or or_1 (or_1_out, A, B);
  main main_1 (.Entrada_A(A), .Entrada_B(B), .out_4(main_1_out_4), .COut(main_1_cout), .CIn(in_3));
  main main_2 (.Entrada_A(A), .Entrada_B(not_1_out), .out_4(main_2_out_4), .COut(main_2_cout), .CIn(in_3));
  Multiplexer multiplexer_1 (.in0(main_1_cout), .in1(main_2_cout), .out(out_6), .sel(in_4[0]));  // open: en
  Multiplexer #(.select(2)) multiplexer_2 (
    .in0(and_1_out), .in1(or_1_out), .in2(main_1_out_4), .in3(main_2_out_4), .out(out_5), .sel(in_4));  // open: en
endmodule

module \ALU_8_bits_con_sustracción  (
  input  [7:0] in_1,
  input  in_2,
  input  [1:0] in_3,
  input  [7:0] in_4,
  output [7:0] out_5,
  output out_6
);

  wire \alu_1_bit_con_sustracción_1_out_6 , \alu_1_bit_con_sustracción_2_out_6 ,
       \alu_1_bit_con_sustracción_3_out_6 , \alu_1_bit_con_sustracción_4_out_6 ,
       \alu_1_bit_con_sustracción_5_out_6 , \alu_1_bit_con_sustracción_6_out_6 ,
       \alu_1_bit_con_sustracción_7_out_6 , or_1_out;

  or or_1 (or_1_out, in_2, in_3[0]);
  \ALU_1_bit_con_sustracción  \alu_1_bit_con_sustracción_1  (
    .out_5(out_5[0]), .out_6(\alu_1_bit_con_sustracción_1_out_6 ), .A(in_4[0]), .B(in_1[0]), .in_3(or_1_out),
    .in_4(in_3));
  \ALU_1_bit_con_sustracción  \alu_1_bit_con_sustracción_2  (
    .out_5(out_5[1]), .out_6(\alu_1_bit_con_sustracción_2_out_6 ), .A(in_4[1]), .B(in_1[1]),
    .in_3(\alu_1_bit_con_sustracción_1_out_6 ), .in_4(in_3));
  \ALU_1_bit_con_sustracción  \alu_1_bit_con_sustracción_3  (
    .out_5(out_5[2]), .out_6(\alu_1_bit_con_sustracción_3_out_6 ), .A(in_4[2]), .B(in_1[2]),
    .in_3(\alu_1_bit_con_sustracción_2_out_6 ), .in_4(in_3));
  \ALU_1_bit_con_sustracción  \alu_1_bit_con_sustracción_4  (
    .out_5(out_5[3]), .out_6(\alu_1_bit_con_sustracción_4_out_6 ), .A(in_4[3]), .B(in_1[3]),
    .in_3(\alu_1_bit_con_sustracción_3_out_6 ), .in_4(in_3));
  \ALU_1_bit_con_sustracción  \alu_1_bit_con_sustracción_5  (
    .out_5(out_5[4]), .out_6(\alu_1_bit_con_sustracción_5_out_6 ), .A(in_4[4]), .B(in_1[4]),
    .in_3(\alu_1_bit_con_sustracción_4_out_6 ), .in_4(in_3));
  \ALU_1_bit_con_sustracción  \alu_1_bit_con_sustracción_6  (
    .out_5(out_5[5]), .out_6(\alu_1_bit_con_sustracción_6_out_6 ), .A(in_4[5]), .B(in_1[5]),
    .in_3(\alu_1_bit_con_sustracción_5_out_6 ), .in_4(in_3));
  \ALU_1_bit_con_sustracción  \alu_1_bit_con_sustracción_7  (
    .out_5(out_5[6]), .out_6(\alu_1_bit_con_sustracción_7_out_6 ), .A(in_4[6]), .B(in_1[6]),
    .in_3(\alu_1_bit_con_sustracción_6_out_6 ), .in_4(in_3));
  \ALU_1_bit_con_sustracción  \alu_1_bit_con_sustracción_8  (
    .out_5(out_5[7]), .out_6(out_6), .A(in_4[7]), .B(in_1[7]), .in_3(\alu_1_bit_con_sustracción_7_out_6 ),
    .in_4(in_3));
endmodule

module Igualdad (
  input  A,
  input  B,
  input  in_3,
  input  [2:0] in_4,
  output out_5,
  output out_6
);

  wire and_1_out, main_1_cout, main_1_out_4, main_2_cout, main_2_out_4, not_1_out, not_2_out, or_1_out;

  not not_1 (not_1_out, B);
  and and_1 (and_1_out, A, B);
  or or_1 (or_1_out, A, B);
  main main_1 (.Entrada_A(A), .Entrada_B(B), .out_4(main_1_out_4), .COut(main_1_cout), .CIn(in_3));
  main main_2 (.Entrada_A(A), .Entrada_B(not_1_out), .out_4(main_2_out_4), .COut(main_2_cout), .CIn(in_3));
  Multiplexer multiplexer_1 (.in0(main_1_cout), .in1(main_2_cout), .out(out_6), .sel(in_4[0]));  // open: en
  not not_2 (not_2_out, main_2_out_4);
  Multiplexer #(.select(3)) multiplexer_2 (
    .in0(and_1_out), .in1(or_1_out), .in2(main_1_out_4), .in3(main_2_out_4), .in4(not_2_out), .out(out_5),
    .sel(in_4));  // open: in5, in6, in7, en
endmodule
