// Logisim project practica3.circ as structural Verilog: 3 circuits, main circuit main
module main (
  input  in_1,
  input  in_2,
  input  in_3,
  input  [1:0] in_4,
  input  in_5,
  input  [1:0] in_6,
  input  [7:0] in_7,
  input  [7:0] in_8,
  input  [7:0] in_9,
  output out_10,
  output out_11,
  output out_12
);

  wire adder_1_out, alu_1_bit_1_out_6, alu_1_bit_2_out_6, alu_1_bit_3_out_6, alu_1_bit_4_out_6,
       alu_1_bit_5_out_6, alu_1_bit_6_out_6, alu_1_bit_7_out_6, and_1_out, or_1_out;
  wire [7:0] alu_1_bit_1_out_5;

  and and_1 (and_1_out, in_2, in_3);
  or or_1 (or_1_out, in_2, in_3);
  Adder #(.width(1)) adder_1 (.a(in_2), .b(in_3), .out(adder_1_out), .cin(in_1), .cout(out_11));
  Multiplexer #(.select(2)) multiplexer_1 (
    .in0(and_1_out), .in1(or_1_out), .in2(adder_1_out), .out(out_10), .sel(in_4));  // open: in3, en
  ALU_1_bit alu_1_bit_1 (
    .out_5(alu_1_bit_1_out_5[0]), .in_2(in_5), .in_3(in_8[0]), .in_1(in_9[0]), .out_6(alu_1_bit_1_out_6),
    .in_4(in_6));
  ALU_1_bit alu_1_bit_2 (
    .out_5(alu_1_bit_1_out_5[1]), .in_2(alu_1_bit_1_out_6), .in_3(in_8[1]), .in_1(in_9[1]),
    .out_6(alu_1_bit_2_out_6), .in_4(in_6));
  ALU_1_bit alu_1_bit_3 (
    .out_5(alu_1_bit_1_out_5[2]), .in_2(alu_1_bit_2_out_6), .in_3(in_8[2]), .in_1(in_9[2]),
    .out_6(alu_1_bit_3_out_6), .in_4(in_6));
  ALU_1_bit alu_1_bit_4 (
    .out_5(alu_1_bit_1_out_5[3]), .in_2(alu_1_bit_3_out_6), .in_3(in_8[3]), .in_1(in_9[3]),
    .out_6(alu_1_bit_4_out_6), .in_4(in_6));
  ALU_1_bit alu_1_bit_5 (
    .out_5(alu_1_bit_1_out_5[4]), .in_2(alu_1_bit_4_out_6), .in_3(in_8[4]), .in_1(in_9[4]),
    .out_6(alu_1_bit_5_out_6), .in_4(in_6));
  ALU_1_bit alu_1_bit_6 (
    .out_5(alu_1_bit_1_out_5[5]), .in_2(alu_1_bit_5_out_6), .in_3(in_8[5]), .in_1(in_9[5]),
    .out_6(alu_1_bit_6_out_6), .in_4(in_6));
  ALU_1_bit alu_1_bit_7 (
    .out_5(alu_1_bit_1_out_5[6]), .in_2(alu_1_bit_6_out_6), .in_3(in_8[6]), .in_1(in_9[6]),
    .out_6(alu_1_bit_7_out_6), .in_4(in_6));
  ALU_1_bit alu_1_bit_8 (
    .out_5(alu_1_bit_1_out_5[7]), .in_2(alu_1_bit_7_out_6), .in_3(in_8[7]), .in_1(in_9[7]), .out_6(out_12),
    .in_4(in_6));

  // Notes on the sheet:
  //   ALU de 1 Bit
endmodule

module ALU_1_bit (
  input  in_1,
  input  in_2,
  input  in_3,
  input  [1:0] in_4,
  output out_5,
  output out_6
);

  wire adder_1_out, and_1_out, or_1_out;

  and and_1 (and_1_out, in_2, in_3);
  or or_1 (or_1_out, in_2, in_3);
  Adder #(.width(1)) adder_1 (.a(in_2), .b(in_3), .out(adder_1_out), .cin(in_1), .cout(out_6));
  Multiplexer #(.select(2)) multiplexer_1 (
    .in0(and_1_out), .in1(or_1_out), .in2(adder_1_out), .out(out_5), .sel(in_4));  // open: in3, en
endmodule

module ALU_8_bits (
  input  in_1,
  input  [1:0] in_2,
  input  [7:0] in_3,
  input  [7:0] in_4,
  input  [7:0] in_5,
  output out_6
);

  wire alu_1_bit_1_out_6, alu_1_bit_2_out_6, alu_1_bit_3_out_6, alu_1_bit_4_out_6, alu_1_bit_5_out_6,
       alu_1_bit_6_out_6, alu_1_bit_7_out_6;
  wire [7:0] alu_1_bit_1_out_5;

  ALU_1_bit alu_1_bit_1 (
    .out_5(alu_1_bit_1_out_5[0]), .in_2(in_1), .in_3(in_4[0]), .in_1(in_5[0]), .out_6(alu_1_bit_1_out_6),
    .in_4(in_2));
  ALU_1_bit alu_1_bit_2 (
    .out_5(alu_1_bit_1_out_5[1]), .in_2(alu_1_bit_1_out_6), .in_3(in_4[1]), .in_1(in_5[1]),
    .out_6(alu_1_bit_2_out_6), .in_4(in_2));
  ALU_1_bit alu_1_bit_3 (
    .out_5(alu_1_bit_1_out_5[2]), .in_2(alu_1_bit_2_out_6), .in_3(in_4[2]), .in_1(in_5[2]),
    .out_6(alu_1_bit_3_out_6), .in_4(in_2));
  ALU_1_bit alu_1_bit_4 (
    .out_5(alu_1_bit_1_out_5[3]), .in_2(alu_1_bit_3_out_6), .in_3(in_4[3]), .in_1(in_5[3]),
    .out_6(alu_1_bit_4_out_6), .in_4(in_2));
  ALU_1_bit alu_1_bit_5 (
    .out_5(alu_1_bit_1_out_5[4]), .in_2(alu_1_bit_4_out_6), .in_3(in_4[4]), .in_1(in_5[4]),
    .out_6(alu_1_bit_5_out_6), .in_4(in_2));
  ALU_1_bit alu_1_bit_6 (
    .out_5(alu_1_bit_1_out_5[5]), .in_2(alu_1_bit_5_out_6), .in_3(in_4[5]), .in_1(in_5[5]),
    .out_6(alu_1_bit_6_out_6), .in_4(in_2));
  ALU_1_bit alu_1_bit_7 (
    .out_5(alu_1_bit_1_out_5[6]), .in_2(alu_1_bit_6_out_6), .in_3(in_4[6]), .in_1(in_5[6]),
    .out_6(alu_1_bit_7_out_6), .in_4(in_2));
  ALU_1_bit alu_1_bit_8 (
    .out_5(alu_1_bit_1_out_5[7]), .in_2(alu_1_bit_7_out_6), .in_3(in_4[7]), .in_1(in_5[7]), .out_6(out_6),
    .in_4(in_2));
endmodule
