// Logisim project practica2.circ as structural Verilog: 1 circuit, main circuit main
module main (
  input  A,
  input  A_2,
  input  B,
  input  C,
  input  B_2,
  input  A_3,
  input  B_3,
  input  C_2,
  input  D,
  input  A_4,
  input  B_4,
  input  C_3,
  input  D_2,
  input  A_5,
  input  B_5,
  input  C_4,
  input  D_3,
  output out_18,
  output out_19,
  output out_20,
  output out_21,
  output X,
  output Y,
  output Z
);

  wire and_1_out, and_2_out, and_3_out, and_4_out, and_5_out, and_6_out, and_7_out, and_8_out, and_9_out,
       and_10_out, and_11_out, and_12_out, and_13_out, and_14_out, and_15_out, and_16_out, and_17_out,
       and_18_out, and_19_out, and_20_out, and_21_out, and_22_out, and_23_out, not_1_out, not_2_out,
       not_3_out, not_4_out, not_5_out, not_6_out, not_7_out, not_8_out, not_9_out, not_10_out, not_11_out,
       not_12_out, not_13_out, not_14_out, not_15_out, or_4_out, or_5_out, transistor_1_out;

  not not_1 (not_1_out, A_3);
  Transistor transistor_1 (.in(1'b0), .out(transistor_1_out), .gate(B_2));
  Transistor #(.\type ("n")) transistor_2 (.in(1'b1), .out(transistor_1_out), .gate(B_2));
  not not_2 (not_2_out, B_3);
  not not_3 (not_3_out, A_5);
  not not_4 (not_4_out, B_5);
  Transistor transistor_3 (.in(1'b1), .out(out_18), .gate(A));
  Transistor #(.\type ("n")) transistor_4 (.in(transistor_1_out), .out(out_18), .gate(A));
  not not_5 (not_5_out, C_2);
  not not_6 (not_6_out, C_4);
  not not_7 (not_7_out, D);
  not not_8 (not_8_out, D_3);
  and and_1 (and_1_out, not_3_out, C_4);
  and and_2 (and_2_out, not_3_out, not_4_out, D_3);
  and and_3 (and_3_out, not_4_out, C_4, D_3);
  and and_4 (and_4_out, not_3_out, not_4_out, C_4);
  and and_5 (and_5_out, not_3_out, C_4, D_3);
  and and_6 (and_6_out, A_5, B_5, not_6_out);
  and and_7 (and_7_out, A_5, not_6_out, not_8_out);
  and and_8 (and_8_out, not_4_out, D_3);
  and and_9 (and_9_out, B_5, not_8_out);
  not not_9 (not_9_out, A_2);
  and and_10 (and_10_out, not_1_out, not_2_out, not_5_out, D);
  and and_11 (and_11_out, not_1_out, not_2_out, C_2, not_7_out);
  and and_12 (and_12_out, not_1_out, not_2_out, C_2, D);
  and and_13 (and_13_out, not_1_out, B_3, C_2, not_7_out);
  and and_14 (and_14_out, not_1_out, B_3, C_2, D);
  and and_15 (and_15_out, A_3, not_2_out, C_2, D);
  not not_10 (not_10_out, B);
  or or_1 (X, and_1_out, and_2_out, and_3_out);
  or or_2 (Y, and_4_out, and_5_out, and_6_out, and_7_out);
  or or_3 (Z, and_8_out, and_9_out);
  not not_11 (not_11_out, C);
  or or_4 (or_4_out, and_10_out, and_11_out, and_12_out, and_13_out, and_14_out);
  buf or_5 (or_5_out, and_15_out);  // OR_Gate
  and and_16 (and_16_out, not_9_out, B, not_11_out);
  and and_17 (and_17_out, not_9_out, B, C);
  and and_18 (and_18_out, A_2, not_10_out, C);
  and and_19 (and_19_out, A_2, B, C);
  or or_6 (out_21, or_4_out, or_5_out);
  or or_7 (out_19, and_16_out, and_17_out, and_18_out, and_19_out);
  not not_12 (not_12_out, A_4);
  not not_13 (not_13_out, B_4);
  not not_14 (not_14_out, C_3);
  not not_15 (not_15_out, D_2);
  and and_20 (and_20_out, not_12_out, not_13_out, not_14_out, not_15_out);
  and and_21 (and_21_out, not_12_out, B_4, not_14_out, D_2);
  and and_22 (and_22_out, A_4, not_13_out, C_3, not_15_out);
  and and_23 (and_23_out, A_4, B_4, C_3, D_2);
  or or_8 (out_20, and_20_out, and_21_out, and_22_out, and_23_out);

  // Notes on the sheet:
  //   1) Implicación Lógica
  //   3) x < y
  //   4) Elevador
  //   2) Números Primos
  //   Salida X: Nos inica si el elvador sube (1) y si baja o se queda en el mismo piso (0)
  //   Salidas Y y Z: nos indican el número de pisos que nos hemos desplazado, dependiendo el caso en las entradas A y B
  //   3) x = y
endmodule
